// Logisim project ex4.circ as structural Verilog: 5 circuits, main circuit RotRight
module RotRight (
  input  [15:0] INPUT0,
  input  [3:0] AMOUNT,
  output [15:0] OUTPUT0
);

  wire [15:0] rot1_1_out_2, rot1_3_out_2, rot1_4_out_2, rot1_5_out_2, rot1_6_out_2, rot1_7_out_2,
       rot2_1_out_2, rot2_2_out_2, rot4_2_out_2;

  rot1 rot1_1 (.in_1(INPUT0), .out_2(rot1_1_out_2));
  rot2 rot2_1 (.in_1(INPUT0), .out_2(rot2_1_out_2));
  rot4 rot4_1 (.in_1(INPUT0), .out_2(rot2_1_out_2));
  rot8 rot8_1 (.in_1(INPUT0), .out_2(rot2_1_out_2));
  rot2 rot2_2 (.in_1(rot1_1_out_2), .out_2(rot2_2_out_2));
  rot4 rot4_2 (.in_1(rot2_1_out_2), .out_2(rot4_2_out_2));
  rot1 rot1_2 (.in_1(rot2_1_out_2), .out_2(rot2_2_out_2));
  rot1 rot1_3 (.in_1(rot2_1_out_2), .out_2(rot1_3_out_2));
  rot4 rot4_3 (.in_1(rot2_1_out_2), .out_2(rot2_2_out_2));
  rot1 rot1_4 (.in_1(rot1_3_out_2), .out_2(rot1_4_out_2));
  rot1 rot1_5 (.in_1(rot2_2_out_2), .out_2(rot1_5_out_2));
  rot1 rot1_6 (.in_1(rot4_2_out_2), .out_2(rot1_6_out_2));
  rot1 rot1_7 (.in_1(rot1_5_out_2), .out_2(rot1_7_out_2));
  rot1 rot1_8 (.in_1(rot1_4_out_2));  // open: out_2
  rot1 rot1_9 (.in_1(rot1_7_out_2));  // open: out_2
  Multiplexer #(.select(4), .width(16)) multiplexer_1 (
    .in0(INPUT0), .in1(rot1_1_out_2), .in2(rot2_1_out_2), .in3(rot2_2_out_2), .in4(rot2_1_out_2),
    .in5(rot2_2_out_2), .in6(rot4_2_out_2), .in7(rot1_6_out_2), .sel(AMOUNT));  // open: in8, in9, in10, in11, in12, in13, in14, in15, out
endmodule

module rot1 (
  input  [15:0] in_1,
  output [15:0] out_2
);


  assign out_2 = {in_1[0], in_1[15:1]};
endmodule

module rot2 (
  input  [15:0] in_1,
  output [15:0] out_2
);


  assign out_2 = {in_1[1:0], in_1[15:2]};
endmodule

module rot4 (
  input  [15:0] in_1,
  output [15:0] out_2
);


  assign out_2 = {in_1[3:0], in_1[15:4]};
endmodule

module rot8 (
  input  [15:0] in_1,
  output [15:0] out_2
);


  assign out_2 = {in_1[7:0], in_1[15:8]};
endmodule
